# Fritzing sketch Schéma 2 (saved by Fritzing 0.9.3b)
breadboards: 1

parts:
  Composant4 = Arduino Uno (Rev3)  # not connected
  Composant5 = Rotoshield - Motor driver shield for Arduino
  M3 = DC Motor
  M4 = DC Motor
  R7 = Resistor [tolerance=±5% resistance=1k package=THT]
  R8 = Resistor [tolerance=±5% resistance=1k package=THT]
  hc-sr3 = hc-sr04
  hc-sr4 = hc-sr04
  R9 = Resistor [tolerance=±5% resistance=1k package=THT]
  Composant6 = Bluetooth HC-05 Macho
  U2 = LIPO-1000mAh [package=lipo-1000]

nets:
  N1: Composant5.DIG_3, R7.Pin_1, R9.Pin_1
  N2: Composant5.DIG_4, Composant6.TXD
  N3: Composant5.DIG_6, hc-sr4.Trig
  N4: Composant5.DIG_7, hc-sr4.Echo
  N5: Composant5.DIG_8, hc-sr3.Trig
  N6: Composant5.DIG_9, hc-sr3.Echo
  VCC: Composant5.+5V, hc-sr3.VCC, hc-sr4.VCC, Composant6.VCC
  GND: Composant5.GND, R8.Pin_0, hc-sr3.GND, hc-sr4.GND, Composant6.GND, U2.-
  N7: Composant5.M1-2, M3.pin_2
  N8: Composant5.M1-1, M3.pin_1
  N9: Composant5.M2-2, M4.pin_2
  N10: Composant5.M2-1, M4.pin_1
  N11: Composant5.VCC, U2.+
  N12: R7.Pin_0, Composant6.RXD
  N13: R8.Pin_1, R9.Pin_0

notes:
  Batterie Li-Po
  7.4 v
  1000 mAh
  POWER BANK
  Les 3 résistances sont de 1k ohms
  Capteurs à ultrasons
  Module bluetooth
  Capteur à ultrasons echo pin 6
  trig pin 7
  echo pin 8
  trig pin 9
  Module bluetooth Rx pin 3
  Tx pin 4
